// Logisim project 4.2 Triplet XOR implemented with only OR.circ as structural Verilog: 1 circuit, main circuit main
module main (
  input  \输入A ,
  input  \输入B ,
  input  \输入C ,
  output \输出F 
);

  wire G1_out, G2_out, G3_out, G4_out, G5_out, G6_out;

  nor G1 (G1_out, \输入A , \输入B );
  nor G2 (G2_out, \输入A , G1_out);
  nor G3 (G3_out, G1_out, \输入B );
  nor G4 (G4_out, G2_out, G3_out, \输入C );
  nor G5 (G5_out, G2_out, G3_out, G4_out);
  nor G6 (G6_out, G4_out, \输入C );
  nor G7 (\输出F , G5_out, G6_out);

  // Notes on the sheet:
  //   F=A⊕B⊕/C
  //   功能：判断输入‘1’的个数。奇数个输出‘1’，偶数个输出‘0’。
endmodule
