// Logisim project 4.2 Triplet XOR.circ as structural Verilog: 1 circuit, main circuit main
module main (
  input  \输入A ,
  input  \输入B ,
  input  \输入C ,
  output \输出F 
);

  wire not_1_out;

  not not_1 (not_1_out, \输入C );
  ExactlyOne xor_1 (.out(\输出F ), .in0(\输入A ), .in1(\输入B ), .in2(not_1_out));

  // Notes on the sheet:
  //   F=A⊕B⊕/C
endmodule
