// Logisim project 4.9 Input count.circ as structural Verilog: 1 circuit, main circuit main
module main (
  input  input_A1,
  input  input_A2,
  input  input_A3,
  input  input_A4,
  output output_F
);

  wire G1_out, G2_out;

  xor G1 (G1_out, input_A1, input_A2);
  xor G2 (G2_out, input_A3, input_A4);
  xnor G3 (output_F, G1_out, G2_out);

  // Notes on the sheet:
  //   Check if there are odd inputs, out put '1' if True, else false
  //   F=(A1⊕A2)⊙(A3⊕A4)
endmodule
