// Logisim project 5.15 8421 Base-10 counter.circ as structural Verilog: 1 circuit, main circuit main
// 8421码十进制加1计数器
module main (
  input  in_1,
  input  _1,
  output Y4_T4__y4y4_y3y2y1_____2_3,
  output Y3_T3__y2y1_____2_2,
  output Y2_T2__ny4y1_____2_1,
  output Y1_T1_1____2_0
);

  wire and_1_out, and_2_out, and_3_out, and_4_out, or_1_out, T4_q;

  and and_1 (and_1_out, Y1_T1_1____2_0, Y2_T2__ny4y1_____2_1, Y3_T3__y2y1_____2_2);
  and and_2 (and_2_out, Y1_T1_1____2_0, Y4_T4__y4y4_y3y2y1_____2_3);
  or or_1 (or_1_out, and_1_out, and_2_out);
  and and_3 (and_3_out, Y1_T1_1____2_0, Y2_T2__ny4y1_____2_1);
  and and_4 (and_4_out, T4_q, Y1_T1_1____2_0);
  T_Flip_Flop T4 (.clk(in_1), .T(or_1_out), .Q(T4_q), .Qn(Y4_T4__y4y4_y3y2y1_____2_3));  // open: preset, reset, en
  T_Flip_Flop T3 (.clk(in_1), .T(and_3_out), .Qn(Y3_T3__y2y1_____2_2));  // open: Q, preset, reset, en
  T_Flip_Flop T2 (.clk(in_1), .T(and_4_out), .Qn(Y2_T2__ny4y1_____2_1));  // open: Q, preset, reset, en
  T_Flip_Flop T1 (.clk(in_1), .T(_1), .Qn(Y1_T1_1____2_0));  // open: Q, preset, reset, en

  // Notes on the sheet:
  //   8421 Code Base 10 add-1 counter
endmodule
