// Logisim project 5.5 Base-3 counter.circ as structural Verilog: 1 circuit, main circuit main
module main (
  input  x,
  input  CP,
  output Z_y1y2_x__y1_y2x
);

  wire and_1_out, and_2_out, and_3_out, and_4_out, nand_1_out, not_1_out, or_1_out, T1_q, T1_qn, T2_q, T2_qn,
       xor_1_out;

  not not_1 (not_1_out, x);
  and and_1 (and_1_out, x, T1_q);
  or or_1 (or_1_out, and_1_out, and_2_out);
  and and_2 (and_2_out, not_1_out, T1_qn, T2_q);
  nand nand_1 (nand_1_out, T1_qn, xor_1_out);
  xor xor_1 (xor_1_out, T2_qn, x);
  and and_3 (and_3_out, T2_qn, T1_qn, not_1_out);
  and and_4 (and_4_out, T2_q, T1_q, x);
  D_Flip_Flop T2 (.clk(CP), .D(or_1_out), .Q(T2_q), .Qn(T2_qn));  // open: preset, en, reset
  D_Flip_Flop T1 (.clk(CP), .D(nand_1_out), .Q(T1_q), .Qn(T1_qn));  // open: preset, en, reset
  or or_2 (Z_y1y2_x__y1_y2x, and_3_out, and_4_out);

  // Notes on the sheet:
  //   Base-3 counter, count if x=1, else countdown
endmodule
