// Logisim project 6.3 input sequence detector.circ as structural Verilog: 1 circuit, main circuit main
module main (
  input  x2,
  input  x1,
  input  x0
);

  wire and_1_out, and_2_out, and_3_out, and_4_out, clock_1_out, or_1_out, or_2_out, y0_q, y0_qn, y1_q, y1_qn;

  and and_1 (and_1_out, y0_q, x1, y1_qn);
  Clock clock_1 (.out(clock_1_out));
  or or_1 (or_1_out, and_2_out, and_3_out, x2);
  and and_2 (and_2_out, x0, y0_qn);
  S_R_Flip_Flop y1 (.S(and_1_out), .clk(clock_1_out), .R(or_1_out), .Q(y1_q), .Qn(y1_qn));  // open: preset, reset, en
  or or_2 (or_2_out, and_3_out, x0);
  and and_3 (and_3_out, x1, y1_q);
  S_R_Flip_Flop y0 (.S(x2), .clk(clock_1_out), .R(or_2_out), .Q(y0_q), .Qn(y0_qn));  // open: preset, reset, en
  and and_4 (and_4_out, y0_qn, y1_q);
  LED z (.in(and_4_out));

  // Notes on the sheet:
  //   x2-x1-x0 input sequence detector
endmodule
