// Logisim project 6.5 3-bit countdown.circ as structural Verilog: 1 circuit, main circuit main
module main (
  output Z
);

  wire and_1_out, D0_q, D0_qn, D1_q, D1_qn, D2_q, D2_qn, X_out;

  and and_1 (and_1_out, D0_qn, D1_qn);
  Button X (.out(X_out));
  D_Flip_Flop #(.trigger("falling")) D2 (.clk(and_1_out), .D(D2_qn), .Q(D2_q), .Qn(D2_qn));  // open: preset, en, reset
  D_Flip_Flop #(.trigger("falling")) D1 (.clk(D0_qn), .D(D1_qn), .Q(D1_q), .Qn(D1_qn));  // open: preset, en, reset
  D_Flip_Flop #(.trigger("falling")) D0 (.clk(X_out), .D(D0_qn), .Q(D0_q), .Qn(D0_qn));  // open: preset, en, reset
  and and_2 (Z, D2_q, D1_q, D0_q, X_out);

  // Notes on the sheet:
  //   3-bit base-2 countdown
endmodule
