// Logisim project 1.1 1-bit half adder.circ as structural Verilog: 1 circuit, main circuit main
module main (
  input  A,
  input  B,
  output S_A_B,
  output C_AB
);

  xor xor_1 (S_A_B, A, B);
  and and_1 (C_AB, A, B);

  // Notes on the sheet:
  //   1-bit half adder
endmodule
