// Logisim project 1.2 1-bit full adder.circ as structural Verilog: 1 circuit, main circuit main
module main (
  input  C1,
  input  A,
  input  B,
  output S_A_B_C1,
  output C__A_B_C1_AB
);

  wire and_1_out, and_2_out, xor_1_out;

  xor xor_1 (xor_1_out, A, B);
  and and_1 (and_1_out, A, B);
  and and_2 (and_2_out, C1, xor_1_out);
  xor xor_2 (S_A_B_C1, C1, xor_1_out);
  or or_1 (C__A_B_C1_AB, and_2_out, and_1_out);

  // Notes on the sheet:
  //   1-bit full adder
endmodule
