// Logisim project 1.5 Carry-lookahead parallel adder.circ as structural Verilog: 2 circuits, main circuit main
module main (
  input  C0,
  input  A4,
  input  A3,
  input  A2,
  input  A1,
  input  B4,
  input  B3,
  input  B2,
  input  B1,
  output C4_P4P3P2P1C0_P4P3P2G1_P4P3G2_P4G3_G4,
  output S4_P4__P3P2P1C0_P3P2G1_P3G2_G3,
  output S3_P3__P2P1C0_P2G1_G2,
  output S2_P2__P1C0_G1,
  output S1_P1_C0
);

  wire C1_out, C2_out, C3_out, G1_out, G2_out, G3_out, G4_out, P1_out, P1C0_out, P2_out, P2G1_out,
       P2P1C0_out, P3_out, P3G2_out, P3P2G1_out, P3P2P1C0_out, P4_out, P4G3_out, P4P3G2_out, P4P3P2G1_out,
       P4P3P2P1C0_out;

  and P4P3G2 (P4P3G2_out, P4_out, P3G2_out);
  and P4G3 (P4G3_out, P4_out, G3_out);
  or C4 (C4_P4P3P2P1C0_P4P3P2G1_P4P3G2_P4G3_G4, G4_out, P4G3_out, P4P3G2_out, P4P3P2G1_out, P4P3P2P1C0_out);
  and P4P3P2P1C0 (P4P3P2P1C0_out, P4_out, P3P2P1C0_out);
  and P4P3P2G1 (P4P3P2G1_out, P4_out, P3P2G1_out);
  xor P4 (P4_out, A4, B4);
  and G4 (G4_out, A4, B4);
  xor xor_1 (S4_P4__P3P2P1C0_P3P2G1_P3G2_G3, P4_out, C3_out);
  or C3 (C3_out, G3_out, P3G2_out, P3P2G1_out, P3P2P1C0_out);
  and P3G2 (P3G2_out, P3_out, G2_out);
  and G3 (G3_out, A3, B3);
  xor xor_2 (S3_P3__P2P1C0_P2G1_G2, P3_out, C2_out);
  and P3P2P1C0 (P3P2P1C0_out, P3_out, P2P1C0_out);
  and P3P2G1 (P3P2G1_out, P3_out, P2G1_out);
  xor P3 (P3_out, A3, B3);
  or C2 (C2_out, G2_out, P2G1_out, P2P1C0_out);
  and P2G1 (P2G1_out, P2_out, G1_out);
  and G2 (G2_out, A2, B2);
  xor xor_3 (S2_P2__P1C0_G1, P2_out, C1_out);
  and P2P1C0 (P2P1C0_out, P2_out, P1C0_out);
  xor P2 (P2_out, A2, B2);
  xor xor_4 (S1_P1_C0, P1_out, C0);
  or C1 (C1_out, G1_out, P1C0_out);
  and P1C0 (P1C0_out, P1_out, C0);
  xor P1 (P1_out, A1, B1);
  and G1 (G1_out, A1, B1);

  // Notes on the sheet:
  //   Carry-lookahead parallel adder
endmodule

module \封装  (
  input  in_1,
  input  in_2,
  input  in_3,
  input  in_4,
  input  in_5,
  input  in_6,
  input  in_7,
  input  in_8,
  input  in_9,
  output out_10,
  output out_11,
  output out_12,
  output out_13,
  output C4
);

  main main_1 (
    .C4_P4P3P2P1C0_P4P3P2G1_P4P3G2_P4G3_G4(C4), .S4_P4__P3P2P1C0_P3P2G1_P3G2_G3(out_10),
    .S3_P3__P2P1C0_P2G1_G2(out_11), .S2_P2__P1C0_G1(out_12), .S1_P1_C0(out_13), .A4(in_2), .B4(in_6),
    .A3(in_3), .B3(in_7), .A2(in_4), .B2(in_8), .A1(in_5), .B1(in_9), .C0(in_1));
endmodule
