// Logisim project 2.1 4-bit base-2 revertible counter.circ as structural Verilog: 2 circuits, main circuit 4-bit base-2 revertible counter
module _4_bit_base_2_revertible_counter (
  input  CPu,
  input  CPd,
  input  CLR,
  output SA,
  output SB,
  output SC,
  output SD
);

  wire A_qn, and_1_out, and_2_out, and_3_out, and_4_out, and_5_out, and_6_out, and_7_out, and_8_out,
       and_9_out, and_10_out, and_11_out, and_12_out, B_qn, C_qn, or_1_out, or_2_out, or_3_out, or_4_out,
       xor_1_out, xor_2_out, xor_3_out, xor_4_out, xor_5_out, xor_6_out, xor_7_out;

  and and_1 (and_1_out, CPu, A_qn);
  xor xor_1 (xor_1_out, CPu, CPd);
  and and_2 (and_2_out, CPd, A_qn);
  or or_1 (or_1_out, and_1_out, and_2_out);
  xor xor_2 (xor_2_out, SA, SB);
  and and_3 (and_3_out, CPu, xor_2_out);
  D_Flip_Flop #(.trigger("falling")) A (
    .clk(xor_1_out), .D(or_1_out), .Q(SA), .Qn(A_qn), .preset(1'b0), .reset(CLR));  // open: en
  and and_4 (and_4_out, CPd, xor_3_out);
  xor xor_3 (xor_3_out, A_qn, SB);
  D_Flip_Flop #(.trigger("falling")) B (
    .clk(xor_1_out), .D(or_2_out), .Q(SB), .Qn(B_qn), .preset(1'b0), .reset(CLR));  // open: en
  or or_2 (or_2_out, and_3_out, and_4_out);
  and and_5 (and_5_out, SA, SB);
  xor xor_4 (xor_4_out, and_5_out, SC);
  and and_6 (and_6_out, CPu, xor_4_out);
  or or_3 (or_3_out, and_6_out, and_7_out);
  and and_7 (and_7_out, CPd, xor_5_out);
  xor xor_5 (xor_5_out, and_8_out, SC);
  and and_8 (and_8_out, B_qn, A_qn);
  D_Flip_Flop #(.trigger("falling")) C (
    .clk(xor_1_out), .D(or_3_out), .Q(SC), .Qn(C_qn), .preset(1'b0), .reset(CLR));  // open: en
  and and_9 (and_9_out, SC, SB, SA);
  xor xor_6 (xor_6_out, and_9_out, SD);
  and and_10 (and_10_out, CPu, xor_6_out);
  or or_4 (or_4_out, and_10_out, and_11_out);
  and and_11 (and_11_out, CPd, xor_7_out);
  xor xor_7 (xor_7_out, and_12_out, SD);
  and and_12 (and_12_out, C_qn, A_qn, B_qn);
  D_Flip_Flop #(.trigger("falling")) D (
    .clk(xor_1_out), .D(or_4_out), .Q(SD), .preset(1'b0), .reset(CLR));  // open: Qn, en
endmodule

module test (
  input  in_1,
  input  in_2,
  input  in_3,
  output out_4,
  output out_5,
  output out_6,
  output out_7
);

  _4_bit_base_2_revertible_counter u_4_bit_base_2_revertible_counter_1 (
    .SD(out_4), .SA(out_7), .SB(out_6), .SC(out_5), .CPu(in_1), .CPd(in_3), .CLR(in_2));
endmodule
