// Logisim project 2.2 2-bit 8421 code converter.circ as structural Verilog: 3 circuits, main circuit 8421 code converter
module _8421_code_converter (
  input  S4,
  input  S3,
  input  S2,
  input  S1,
  output h4,
  output h3,
  output h2,
  output h1,
  output g4,
  output g3,
  output g2,
  output g1
);

  wire and_1_out, and_2_out, or_1_out;

  _4_bit_base_2_adder u_4_bit_base_2_adder_1 (
    .B3(1'b0), .A3(S4), .B2(or_1_out), .A2(S3), .B1(or_1_out), .A1(S2), .B0(1'b0), .A0(S1), .S3(g4), .S2(g3),
    .S1(g2), .S0(g1), .C4(h1), .C0(1'b0));
  and and_1 (and_1_out, S4, S3);
  or or_1 (or_1_out, and_1_out, and_2_out);
  and and_2 (and_2_out, S4, S2);

  assign h2 = 1'b0;
  assign h3 = 1'b0;
  assign h4 = 1'b0;
endmodule

module _4_bit_base_2_adder (
  input  B3,
  input  A3,
  input  B2,
  input  A2,
  input  B1,
  input  A1,
  input  B0,
  input  A0,
  input  C0,
  output C4,
  output S3,
  output S2,
  output S1,
  output S0
);

  wire and_1_out, and_2_out, and_3_out, and_4_out, and_5_out, and_6_out, and_7_out, and_8_out, and_9_out,
       and_10_out, and_11_out, and_12_out, and_13_out, and_14_out, C1_out, C2_out, C3_out, xor_1_out,
       xor_2_out, xor_3_out, xor_4_out;

  and and_1 (and_1_out, B3, A3);
  xor xor_1 (xor_1_out, B3, A3);
  and and_2 (and_2_out, B2, A2);
  xor xor_2 (xor_2_out, B2, A2);
  and and_3 (and_3_out, B1, A1);
  xor xor_3 (xor_3_out, B1, A1);
  and and_4 (and_4_out, B0, A0);
  xor xor_4 (xor_4_out, B0, A0);
  and and_5 (and_5_out, xor_1_out, and_2_out);
  and and_6 (and_6_out, xor_1_out, xor_2_out, and_3_out);
  and and_7 (and_7_out, xor_1_out, xor_2_out, xor_3_out, and_4_out);
  and and_8 (and_8_out, xor_1_out, xor_2_out, xor_3_out, xor_4_out, C0);
  and and_9 (and_9_out, and_3_out, xor_2_out);
  and and_10 (and_10_out, xor_2_out, xor_3_out, and_4_out);
  and and_11 (and_11_out, xor_2_out, xor_3_out, xor_4_out, C0);
  and and_12 (and_12_out, xor_3_out, and_4_out);
  and and_13 (and_13_out, xor_3_out, xor_4_out, C0);
  and and_14 (and_14_out, xor_4_out, C0);
  or u_C4 (C4, and_5_out, and_6_out, and_7_out, and_8_out, and_1_out);
  or C3 (C3_out, and_9_out, and_2_out, and_10_out, and_11_out);
  or C2 (C2_out, and_3_out, and_12_out, and_13_out);
  or C1 (C1_out, and_4_out, and_14_out);
  xor xor_5 (S3, xor_1_out, C3_out);
  xor xor_6 (S2, xor_2_out, C2_out);
  xor xor_7 (S1, xor_3_out, C1_out);
  xor xor_8 (S0, xor_4_out, C0);
endmodule

module encapsulation (
  input  in_1,
  input  in_2,
  input  in_3,
  input  in_4,
  output out_5,
  output out_6,
  output out_7,
  output out_8,
  output out_9,
  output out_10,
  output out_11,
  output out_12
);

  _8421_code_converter u_8421_code_converter_1 (
    .h4(out_5), .h3(out_6), .h2(out_7), .h1(out_8), .g4(out_9), .g3(out_10), .g2(out_11), .g1(out_12),
    .S4(in_1), .S3(in_2), .S2(in_3), .S1(in_4));
endmodule
