// Logisim project 2.3 Seven-Segment Display.circ as structural Verilog: 2 circuits, main circuit main
module main (
  input  a3,
  input  a2,
  input  a1,
  input  a0,
  output g,
  output f,
  output e,
  output d,
  output c,
  output b,
  output a
);

  wire and_1_out, and_2_out, and_3_out, and_4_out, and_5_out, and_6_out, and_7_out, and_8_out, and_9_out,
       and_10_out, and_11_out, and_12_out, and_13_out, and_14_out, and_15_out, and_16_out, and_17_out,
       not_1_out, not_2_out, not_3_out, not_4_out, or_1_out, or_2_out, or_3_out, or_4_out, or_5_out,
       or_6_out, or_7_out, or_8_out, xor_1_out, xor_2_out;

  or u_g (g, and_2_out, and_1_out);
  and and_1 (and_1_out, not_1_out, a1, or_1_out);
  and and_2 (and_2_out, not_3_out, xor_1_out);
  xor xor_1 (xor_1_out, a3, a2);
  or or_1 (or_1_out, not_2_out, not_4_out);
  or u_f (f, and_4_out, and_3_out);
  and and_3 (and_3_out, not_2_out, not_3_out, or_3_out);
  and and_4 (and_4_out, not_1_out, a2, or_2_out);
  or or_2 (or_2_out, not_3_out, not_4_out);
  or u_e (e, and_5_out, and_7_out);
  or or_3 (or_3_out, a3, not_4_out);
  and and_5 (and_5_out, not_1_out, a1, not_4_out);
  _7_Segment_Display u_7_segment_display_1 (.g(g), .f(f), .a(a), .b(b), .e(e), .d(d), .c(c));  // open: dp
  and and_6 (and_6_out, not_1_out, a1, or_4_out);
  and and_7 (and_7_out, not_2_out, not_3_out, not_4_out);
  or or_4 (or_4_out, not_2_out, not_4_out);
  not not_1 (not_1_out, a3);
  or u_d (d, and_6_out, and_8_out);
  and and_8 (and_8_out, not_3_out, or_5_out);
  or or_5 (or_5_out, and_10_out, and_9_out);
  and and_9 (and_9_out, not_1_out, a2, a0);
  and and_10 (and_10_out, not_2_out, not_4_out);
  not not_2 (not_2_out, a2);
  or u_c (c, and_11_out, and_12_out);
  and and_11 (and_11_out, not_2_out, not_3_out);
  and and_12 (and_12_out, not_1_out, or_6_out);
  or or_6 (or_6_out, a2, a0);
  not not_3 (not_3_out, a1);
  or u_a (a, and_14_out, and_13_out, and_15_out);
  and and_13 (and_13_out, not_1_out, a2, a0);
  and and_14 (and_14_out, not_1_out, a1);
  and and_15 (and_15_out, not_2_out, not_3_out, or_7_out);
  or or_7 (or_7_out, a3, not_4_out);
  not not_4 (not_4_out, a0);
  or u_b (b, and_16_out, and_17_out);
  and and_16 (and_16_out, not_1_out, xor_2_out);
  and and_17 (and_17_out, not_2_out, or_8_out);
  xor xor_2 (xor_2_out, a1, not_4_out);
  or or_8 (or_8_out, not_1_out, not_3_out);
endmodule

module \数码管  (
  input  in_1,
  input  in_2,
  input  in_3,
  input  in_4
);

  wire main_1_a, main_1_b, main_1_c, main_1_d, main_1_e, main_1_f, main_1_g;

  _7_Segment_Display u_7_segment_display_1 (
    .g(main_1_g), .f(main_1_f), .a(main_1_a), .b(main_1_b), .e(main_1_e), .d(main_1_d), .c(main_1_c));  // open: dp
  main main_1 (
    .a3(in_1), .a2(in_2), .a1(in_3), .a0(in_4), .g(main_1_g), .f(main_1_f), .e(main_1_e), .d(main_1_d),
    .c(main_1_c), .b(main_1_b), .a(main_1_a));
endmodule
