// Logisim project 2.5 Access Control System.circ as structural Verilog: 3 circuits, main circuit main
module main (
  input  in_1,
  input  in_2,
  input  in_3,
  output out_4,
  output out_5,
  output out_6,
  output out_7,
  output out_8,
  output out_9,
  output out_10,
  output out_11,
  output out_12,
  output out_13,
  output out_14,
  output out_15,
  output out_16,
  output out_17,
  output Warning
);

  wire and_2_out, and_3_out, n4_bit_base_2_revertible_counter_1_sa, n4_bit_base_2_revertible_counter_1_sb,
       n4_bit_base_2_revertible_counter_1_sc, n4_bit_base_2_revertible_counter_1_sd,
       n8421_code_converter_1_g1, n8421_code_converter_1_g2, n8421_code_converter_1_g3,
       n8421_code_converter_1_g4, n8421_code_converter_1_h1, n8421_code_converter_1_h2,
       n8421_code_converter_1_h3, n8421_code_converter_1_h4, not_1_out;

  and and_1 (Warning, in_1, and_2_out);
  not not_1 (not_1_out, and_2_out);
  _2_3_seven_segment_display_main main_1 (
    .a3(n8421_code_converter_1_h4), .a2(n8421_code_converter_1_h3), .a1(n8421_code_converter_1_h2),
    .a0(n8421_code_converter_1_h1), .g(out_4), .f(out_5), .e(out_6), .d(out_7), .c(out_8), .b(out_9),
    .a(out_10));
  _8421_code_converter u_8421_code_converter_1 (
    .h4(n8421_code_converter_1_h4), .h3(n8421_code_converter_1_h3), .h2(n8421_code_converter_1_h2),
    .h1(n8421_code_converter_1_h1), .g4(n8421_code_converter_1_g4), .g3(n8421_code_converter_1_g3),
    .g2(n8421_code_converter_1_g2), .g1(n8421_code_converter_1_g1),
    .S4(n4_bit_base_2_revertible_counter_1_sd), .S3(n4_bit_base_2_revertible_counter_1_sc),
    .S2(n4_bit_base_2_revertible_counter_1_sb), .S1(n4_bit_base_2_revertible_counter_1_sa));
  and and_2 (and_2_out, n4_bit_base_2_revertible_counter_1_sd, n4_bit_base_2_revertible_counter_1_sc, n4_bit_base_2_revertible_counter_1_sb, n4_bit_base_2_revertible_counter_1_sa);
  and and_3 (and_3_out, not_1_out, in_1);
  _4_bit_base_2_revertible_counter u_4_bit_base_2_revertible_counter_1 (
    .SD(n4_bit_base_2_revertible_counter_1_sd), .SA(n4_bit_base_2_revertible_counter_1_sa),
    .SB(n4_bit_base_2_revertible_counter_1_sb), .SC(n4_bit_base_2_revertible_counter_1_sc), .CPu(and_3_out),
    .CPd(in_3), .CLR(in_2));
  _2_3_seven_segment_display_main main_2 (
    .a3(n8421_code_converter_1_g4), .a2(n8421_code_converter_1_g3), .a1(n8421_code_converter_1_g2),
    .a0(n8421_code_converter_1_g1), .g(out_11), .f(out_12), .e(out_13), .d(out_14), .c(out_15), .b(out_16),
    .a(out_17));
endmodule

module encapsulation (
);

  wire button_1_out, button_2_out, button_3_out, main_1_out_4, main_1_out_5, main_1_out_6, main_1_out_7,
       main_1_out_8, main_1_out_9, main_1_out_10, main_1_out_11, main_1_out_12, main_1_out_13, main_1_out_14,
       main_1_out_15, main_1_out_16, main_1_out_17, main_1_warning;

  Button button_1 (.out(button_1_out));
  Button button_2 (.out(button_2_out));
  Button button_3 (.out(button_3_out));
  _7_Segment_Display u_7_segment_display_1 (
    .g(main_1_out_4), .f(main_1_out_5), .a(main_1_out_10), .b(main_1_out_9), .e(main_1_out_6),
    .d(main_1_out_7), .c(main_1_out_8));  // open: dp
  main main_1 (
    .in_1(button_1_out), .in_2(button_2_out), .in_3(button_3_out), .out_4(main_1_out_4),
    .out_5(main_1_out_5), .out_6(main_1_out_6), .out_7(main_1_out_7), .out_8(main_1_out_8),
    .out_9(main_1_out_9), .out_10(main_1_out_10), .out_11(main_1_out_11), .out_12(main_1_out_12),
    .out_13(main_1_out_13), .out_14(main_1_out_14), .out_15(main_1_out_15), .out_16(main_1_out_16),
    .out_17(main_1_out_17), .Warning(main_1_warning));
  _7_Segment_Display u_7_segment_display_2 (
    .g(main_1_out_11), .f(main_1_out_12), .a(main_1_out_17), .b(main_1_out_16), .e(main_1_out_13),
    .d(main_1_out_14), .c(main_1_out_15));  // open: dp
  LED led_1 (.in(main_1_warning));
endmodule

module pre_encapsulation (
  input  in_1,
  input  in_2,
  input  in_3,
  output out_4,
  output out_5,
  output out_6,
  output out_7,
  output out_8,
  output out_9,
  output out_10,
  output out_11,
  output out_12,
  output out_13,
  output out_14,
  output out_15,
  output out_16,
  output out_17,
  output out_18
);

  main main_1 (
    .in_1(in_1), .in_2(in_2), .in_3(in_3), .out_4(out_4), .out_5(out_5), .out_6(out_6), .out_7(out_7),
    .out_8(out_8), .out_9(out_9), .out_10(out_10), .out_11(out_11), .out_12(out_12), .out_13(out_13),
    .out_14(out_14), .out_15(out_15), .out_16(out_16), .out_17(out_17), .Warning(out_18));
endmodule
