// Logisim project Traffic light controller.circ as structural Verilog: 1 circuit, main circuit main
module main (
  input  in_1,
  input  in_2,
  input  in_3,
  input  in_4,
  input  slowest
);

  wire and_1_out, and_2_out, and_3_out, and_4_out, and_5_out, and_6_out, and_7_out, and_8_out, and_9_out,
       and_10_out, and_11_out, and_12_out, and_13_out, and_14_out, and_15_out, and_16_out, clock_1_out,
       JK1_q, JK1_qn, JK2_q, JK2_qn, JK3_q, JK3_qn, n74163_1_p2, n74163_1_p3, n74163_1_p4, n74163_1_p5,
       not_1_out, or_1_out, or_2_out, or_3_out, or_4_out, or_5_out, or_6_out, or_7_out, or_8_out, or_9_out;

  Clock clock_1 (.out(clock_1_out));
  not not_1 (not_1_out, in_1);
  and and_1 (and_1_out, JK3_q, in_1);
  and and_2 (and_2_out, JK1_qn, in_1);
  and and_3 (and_3_out, JK1_qn, JK2_qn, not_1_out);
  and and_4 (and_4_out, JK1_qn, JK2_q, in_1);
  and and_5 (and_5_out, JK1_q, JK2_qn, in_1);
  // _74163 74163_1: pin names not known; wires that end beside it: clock_1_out, n74163_1_p2, n74163_1_p3, n74163_1_p4, n74163_1_p5
  and and_6 (and_6_out, in_2, n74163_1_p2);
  and and_7 (and_7_out, in_3, n74163_1_p3);
  and and_8 (and_8_out, n74163_1_p4, in_4);
  and and_9 (and_9_out, n74163_1_p5, slowest);
  and and_10 (and_10_out, JK2_q, JK3_q, in_1);
  or or_1 (or_1_out, not_1_out, JK2_q, JK3_q);
  or or_2 (or_2_out, and_1_out, and_2_out);
  or or_3 (or_3_out, JK3_q, not_1_out, JK1_q);
  or or_4 (or_4_out, and_3_out, and_4_out, and_5_out);
  or or_5 (or_5_out, and_6_out, and_7_out, and_8_out, and_9_out);
  J_K_Flip_Flop JK1 (.J(and_10_out), .clk(or_5_out), .K(or_1_out), .Q(JK1_q), .Qn(JK1_qn));  // open: preset, en, reset
  J_K_Flip_Flop JK2 (.J(or_2_out), .clk(or_5_out), .K(or_3_out), .Q(JK2_q), .Qn(JK2_qn));  // open: preset, en, reset
  J_K_Flip_Flop JK3 (.J(or_4_out), .clk(or_5_out), .K(JK3_q), .Q(JK3_q), .Qn(JK3_qn));  // open: preset, en, reset
  and and_11 (and_11_out, JK1_qn, JK3_qn);
  and and_12 (and_12_out, JK2_qn, JK3_qn);
  or or_6 (or_6_out, JK2_q, and_11_out);
  or or_7 (or_7_out, or_6_out, and_13_out);
  and and_13 (and_13_out, JK1_q, JK2_qn, JK3_q);
  and and_14 (and_14_out, JK1_q, JK2_qn, JK3_qn);
  or or_8 (or_8_out, and_12_out, JK1_q);
  or or_9 (or_9_out, or_8_out, and_15_out);
  and and_15 (and_15_out, JK1_qn, JK2_q, JK3_q);
  and and_16 (and_16_out, JK1_qn, JK2_q, JK3_qn);
  LED DW1 (.in(or_7_out));
  LED W1 (.in(and_14_out));
  LED R1 (.in(or_6_out));
  LED Y1 (.in(and_13_out));
  LED G1 (.in(and_14_out));
  LED DW2 (.in(or_9_out));
  LED W2 (.in(and_16_out));
  LED R2 (.in(or_8_out));
  LED Y2 (.in(and_15_out));
  LED G2 (.in(and_16_out));

  // Notes on the sheet:
  //   Mode
  //   Speed
  //   fastest
endmodule
